# Fritzing sketch Miniestação (saved by Fritzing 0.9.3b)
circuit board: 8.65487cm x 5.84698cm
breadboards: 1

parts:
  S1 = Reed switch [package=THT]  # not connected
  LCD1 = LCD screen
  LCM1602_IIC1 = LCM1602 IIC [part_number="LCM1602 IIC" chip_label="LCM1602 IIC" package="DIP (Dual Inline) [THT]"]
  Componente4 = Solar Cell
  microSD1 = MicroSD Card Module
  RTC = Real Time Clock Breakout - DS1307 [part_number=147824]
  S2 = Reed switch [package=THT]
  1K = Resistor [tolerance=±5% resistance=1k package=THT]
  1K_2 = Resistor [tolerance=±5% resistance=1k package=THT]
  10K = Resistor [tolerance=±5% resistance=10k package=THT]
  R1 = PHOTOCELL [package=photocell]
  Componente5 = Arduino Nano (Rev3.0)
  Componente7 = AHT10
  U1 = SWITCH-SPST-2 [package=switch-spst-vertical]

nets:
  VSS: LCD1.VSS, LCM1602_IIC1.VSS
  VDD: LCD1.VDD, LCM1602_IIC1.VDD
  N1: LCD1.V0, LCM1602_IIC1.V0
  N2: LCD1.RS, LCM1602_IIC1.RS
  N3: LCD1.R/W, LCM1602_IIC1.RW
  N4: LCD1.E, LCM1602_IIC1.E
  N5: LCD1.DB0, LCM1602_IIC1.D0
  N6: LCD1.DB1, LCM1602_IIC1.D1
  N7: LCD1.DB2, LCM1602_IIC1.D2
  N8: LCD1.DB3, LCM1602_IIC1.D3
  N9: LCD1.DB4, LCM1602_IIC1.D4
  N10: LCD1.DB5, LCM1602_IIC1.D5
  N11: LCD1.DB6, LCM1602_IIC1.D6
  N12: LCD1.DB7, LCM1602_IIC1.D7
  N13: LCD1.LED+, LCM1602_IIC1.A
  N14: LCD1.LED-, LCM1602_IIC1.K
  GND: LCM1602_IIC1.GND, RTC.GND, S2.pin_2
  N15: LCM1602_IIC1.VCC, U1.O
  N16: Componente4.+, Componente5.VIN
  GND_2: Componente4.-, microSD1.GND, Componente5.GND, Componente7.GND
  VCC: microSD1.VCC, 1K_2.Pin_1, R1.P$1, Componente5.5V
  N17: microSD1.MISO, Componente5.D12/MISO
  N18: microSD1.MOSI, Componente5.D11/MOSI
  N19: microSD1.SCK, Componente5.D13/SCK
  N20: microSD1.CS, Componente5.D10
  N21: RTC.SDA, Componente5.A4
  N22: RTC.VCC, U1.P
  N23: S2.pin_1, 1K_2.Pin_0, Componente5.D5
  N24: 1K.Pin_1, Componente5.D2
  N25: 10K.Pin_0, R1.P$2, Componente5.A0
  N26: Componente5.A5, Componente7.SCL
  3V3: Componente5.3V3, Componente7.VCC

custom parts:
  LCM1602 IIC: I2C-Module to use a 1602 or 2004 LCD on with the wire.h libory Serial LCD Modul
  Real Time Clock Breakout - DS1307: Two wire I2C interface; Hour : Minutes : Seconds AM/PM Day Month, Date - Year; Leap year compensation; Accurate calendar up to year 2100; DS1307 based RTC with LIR2032 battery (Battery include); 56 Bytes of Non-volatile memory available to user; Working time: 1 year
